# Fritzing sketch lampControlWithRaspberry (saved by Fritzing 0.9.6b)
breadboards: 1

parts:
  MCU1 = Raspberry Pi Zero
  CUI-enc1 = AMT103
  R1 = Resistor [tolerance=±5% resistance=220 package="2512 [SMD]"]
  LED1 = smd LED [color="Red (633nm)" package="1206 [SMD]"]
  V1 = DC Power [voltage=12]
  J1 = Screw terminal - 2 pins [package=THT]
  Q1 = Basic FET N-Channel [package="TO220 [THT]"]

nets:
  N1: MCU1.pin_2, MCU1.pin_4, CUI-enc1.5V
  N2: MCU1.pin_11, CUI-enc1.GND
  N3: MCU1.pin_12, LED1.anode, Q1.gate
  N4: MCU1.pin_13, CUI-enc1.X
  N5: MCU1.pin_14, MCU1.pin_20, MCU1.pin_34, MCU1.pin_39, CUI-enc1.B, R1.Pin_1, V1.V-, Q1.source
  N6: MCU1.pin_16, CUI-enc1.A
  N7: R1.Pin_0, LED1.cathode
  N8: V1.V+, J1.pin2
  N9: J1.pin1, Q1.drain
